// Logisim project NAND Gate implementation.circ as structural Verilog: 1 circuit, main circuit main
module main (
  input  in_1,
  input  in_2
);

  wire nand_1_out, undriven, undriven_2;

  nand nand_1 (nand_1_out, undriven, undriven_2);
endmodule
