// Logisim project Task03_NAND_Part.circ as structural Verilog: 2 circuits, main circuit main
module main (
  input  A,
  input  B,
  input  C,
  output F_AC_BC_prime
);

  wire ic7400_1_out_9, ic7400_1_out_10, ic7400_1_out_12, ic7400_2_out_9, ic7400_2_out_10, ic7400_2_out_11,
       ic7400_2_out_12;

  ic7400 ic7400_1 (
    .in_1(A), .in_2(C), .in_3(ic7400_1_out_9), .in_4(ic7400_1_out_9), .in_5(ic7400_1_out_12),
    .in_6(ic7400_2_out_12), .in_7(ic7400_1_out_10), .in_8(ic7400_1_out_10), .out_9(ic7400_1_out_9),
    .out_10(ic7400_1_out_10), .out_11(F_AC_BC_prime), .out_12(ic7400_1_out_12));
  ic7400 ic7400_2 (
    .in_1(C), .in_2(C), .in_3(ic7400_2_out_9), .in_4(B), .in_5(ic7400_2_out_10), .in_6(ic7400_2_out_10),
    .in_7(ic7400_2_out_11), .in_8(ic7400_2_out_11), .out_9(ic7400_2_out_9), .out_10(ic7400_2_out_10),
    .out_11(ic7400_2_out_11), .out_12(ic7400_2_out_12));

  // Notes on the sheet:
  //   C'
  //   AC
  //   BC'
endmodule

module ic7400 (
  input  in_1,
  input  in_2,
  input  in_3,
  input  in_4,
  input  in_5,
  input  in_6,
  input  in_7,
  input  in_8,
  output out_9,
  output out_10,
  output out_11,
  output out_12
);

  nand nand_1 (out_9, in_1, in_2);
  nand nand_2 (out_10, in_3, in_4);
  nand nand_3 (out_11, in_5, in_6);
  nand nand_4 (out_12, in_7, in_8);
endmodule
