// Logisim project Task03_NOR_Part.circ as structural Verilog: 2 circuits, main circuit main
module main (
  input  A,
  input  B,
  input  C,
  output F_AC_BC_prime
);

  wire ic7402_1_out_9, ic7402_1_out_10, ic7402_1_out_11, ic7402_1_out_12, ic7402_2_out_9, ic7402_2_out_10,
       ic7402_2_out_11, ic7402_3_out_9, ic7402_3_out_10;

  ic7402 ic7402_1 (
    .in_1(A), .in_2(A), .in_3(C), .in_4(C), .in_5(C), .in_6(C), .in_7(ic7402_1_out_9),
    .in_8(ic7402_1_out_10), .out_9(ic7402_1_out_9), .out_10(ic7402_1_out_10), .out_11(ic7402_1_out_11),
    .out_12(ic7402_1_out_12));
  ic7402 ic7402_2 (
    .in_1(ic7402_1_out_11), .in_2(ic7402_1_out_11), .in_3(B), .in_4(B), .in_5(ic7402_2_out_9),
    .in_6(ic7402_2_out_10), .out_9(ic7402_2_out_9), .out_10(ic7402_2_out_10), .out_11(ic7402_2_out_11));  // open: in_7, in_8, out_12
  ic7402 ic7402_3 (
    .in_1(ic7402_1_out_12), .in_2(ic7402_2_out_11), .in_3(ic7402_1_out_12), .in_4(ic7402_2_out_11),
    .in_7(ic7402_3_out_9), .in_8(ic7402_3_out_10), .out_9(ic7402_3_out_9), .out_10(ic7402_3_out_10),
    .out_12(F_AC_BC_prime));  // open: in_5, in_6, out_11

  // Notes on the sheet:
  //   C'
  //   AC
  //   BC'
endmodule

module ic7402 (
  input  in_1,
  input  in_2,
  input  in_3,
  input  in_4,
  input  in_5,
  input  in_6,
  input  in_7,
  input  in_8,
  output out_9,
  output out_10,
  output out_11,
  output out_12
);

  nor nor_1 (out_9, in_1, in_2);
  nor nor_2 (out_10, in_3, in_4);
  nor nor_3 (out_11, in_5, in_6);
  nor nor_4 (out_12, in_7, in_8);
endmodule
