// Logisim project implementation of NAND and NOR gates.circ as structural Verilog: 1 circuit, main circuit main
module main (
  input  in_1,
  input  in_2,
  input  in_3,
  input  in_4,
  input  in_5,
  input  in_6,
  input  in_7,
  input  in_8,
  input  in_9,
  input  in_10,
  input  in_11,
  input  in_12,
  input  in_13,
  input  in_14,
  input  in_15,
  output out_16,
  output out_17,
  output out_18,
  output out_19,
  output out_20,
  output out_21,
  output out_22,
  output out_23,
  output out_24
);

  wire nand_1_out, nand_2_out, nand_3_out, nor_2_out, nor_3_out, nor_4_out, nor_5_out;

  nand nand_1 (nand_1_out, in_5, in_7);
  nand nand_2 (nand_2_out, in_11, in_11);
  nand nand_3 (nand_3_out, in_14, in_14);
  nand nand_4 (out_16, in_1, in_1);
  nand nand_5 (out_19, nand_1_out, nand_1_out);
  nand nand_6 (out_23, nand_2_out, nand_3_out);
  not not_1 (out_17, in_2);
  and and_1 (out_20, in_6, in_8);
  or or_1 (out_24, in_12, in_13);
  nor nor_1 (out_18, in_3, in_3);
  nor nor_2 (nor_2_out, in_4, in_4);
  nor nor_3 (nor_3_out, in_9, in_9);
  nor nor_4 (nor_4_out, in_10, in_15);
  nor nor_5 (nor_5_out, in_10, in_15);
  nor nor_6 (out_21, nor_2_out, nor_3_out);
  nor nor_7 (out_22, nor_4_out, nor_5_out);

  // Notes on the sheet:
  //   Equivalent Gates in NAND
  //   Basic Gates
  //   Equivalent Gates in NOR
endmodule
