// Logisim project implementation of XOR and XNOR using NAND and NOR.circ as structural Verilog: 1 circuit, main circuit main
module main (
  input  in_1,
  input  in_2,
  input  in_3,
  input  in_4,
  input  in_5,
  input  in_6,
  input  in_7,
  input  in_8,
  output out_9,
  output out_10,
  output out_11,
  output out_12
);

  wire nand_1_out, nand_2_out, nand_3_out, nand_4_out, nand_5_out, nand_6_out, nand_7_out, nor_1_out,
       nor_2_out, nor_3_out, nor_4_out, nor_5_out, nor_6_out, nor_7_out;

  nand nand_1 (nand_1_out, in_2, in_4);
  nand nand_2 (nand_2_out, in_5, in_8);
  nand nand_3 (nand_3_out, in_5, nand_2_out);
  nand nand_4 (nand_4_out, nand_2_out, in_8);
  nand nand_5 (nand_5_out, in_2, nand_1_out);
  nand nand_6 (nand_6_out, nand_1_out, in_4);
  nand nand_7 (nand_7_out, nand_3_out, nand_4_out);
  nand nand_8 (out_9, nand_5_out, nand_6_out);
  nand nand_9 (out_12, nand_7_out, nand_7_out);
  nor nor_1 (nor_1_out, in_1, in_1);
  nor nor_2 (nor_2_out, in_3, in_3);
  nor nor_3 (nor_3_out, in_1, in_3);
  nor nor_4 (nor_4_out, in_6, in_7);
  nor nor_5 (nor_5_out, nor_1_out, nor_2_out);
  nor nor_6 (nor_6_out, in_6, nor_4_out);
  nor nor_7 (nor_7_out, nor_4_out, in_7);
  nor nor_8 (out_10, nor_5_out, nor_3_out);
  nor nor_9 (out_11, nor_6_out, nor_7_out);

  // Notes on the sheet:
  //   XOR using NAND:
  //   XNOR using NAND:
  //   XOR using NOR:
  //   XNOR using NOR:
endmodule
