// Logisim project 4 output in one subcircuit.circ as structural Verilog: 5 circuits, main circuit main
module main (
  input  W,
  input  X,
  input  Y,
  input  Z,
  output D___Z_prime,
  output C___Y_prime_Z_prime___YZ,
  output out_7,
  output A___W___XZ___XY
);

  wire ic_7404_1_out_7, ic_7404_1_out_8, ic_7408_1_out_9, ic_7408_1_out_10, ic_7408_1_out_11,
       ic_7408_1_out_12, ic_7408_2_out_9, ic_7408_2_out_10, ic_7408_2_out_12;

  ic_7408 ic_7408_1 (
    .in_1(X), .in_2(Z), .in_3(X), .in_4(Y), .in_5(ic_7404_1_out_7), .in_6(Y), .in_7(Z),
    .in_8(ic_7404_1_out_7), .out_9(ic_7408_1_out_9), .out_10(ic_7408_1_out_10), .out_11(ic_7408_1_out_11),
    .out_12(ic_7408_1_out_12));
  ic_4075 ic_4075_1 (
    .in_1(ic_7408_1_out_12), .in_2(ic_7408_1_out_11), .in_3(ic_7408_2_out_10), .in_4(ic_7408_1_out_10),
    .in_5(ic_7408_1_out_9), .in_6(W), .out_10(out_7), .out_11(A___W___XZ___XY));  // open: in_7, in_8, in_9, out_12
  ic_7404 ic_7404_1 (
    .in_1(X), .in_2(Y), .in_3(Z), .out_7(ic_7404_1_out_7), .out_8(ic_7404_1_out_8), .out_9(D___Z_prime));  // open: in_4, in_5, in_6, out_10, out_11, out_12
  ic_7432 ic_7432_1 (
    .in_7(ic_7408_2_out_9), .in_8(ic_7408_2_out_12), .out_12(C___Y_prime_Z_prime___YZ));  // open: in_1, in_2, in_3, in_4, in_5, in_6, out_9, out_10, out_11
  ic_7408 ic_7408_2 (
    .in_1(D___Z_prime), .in_2(ic_7404_1_out_8), .in_3(ic_7408_2_out_9), .in_4(X), .in_7(Y), .in_8(Z),
    .out_9(ic_7408_2_out_9), .out_10(ic_7408_2_out_10), .out_12(ic_7408_2_out_12));  // open: in_5, in_6, out_11

  // Notes on the sheet:
  //   XY
  //   XZ
  //   X'
  //   Z'
  //   Y'
  //   X'Y
  //   X'Z
  //   Y'Z'
  //   XY'Z'
  //   YZ
  //   B = X'Z + X'Y + XY'Z'
endmodule

module ic_4075 (
  input  in_1,
  input  in_2,
  input  in_3,
  input  in_4,
  input  in_5,
  input  in_6,
  input  in_7,
  input  in_8,
  input  in_9,
  output out_10,
  output out_11,
  output out_12
);

  or or_1 (out_10, in_1, in_2, in_3);
  or or_2 (out_11, in_4, in_5, in_6);
  or or_3 (out_12, in_7, in_8, in_9);
endmodule

module ic_7408 (
  input  in_1,
  input  in_2,
  input  in_3,
  input  in_4,
  input  in_5,
  input  in_6,
  input  in_7,
  input  in_8,
  output out_9,
  output out_10,
  output out_11,
  output out_12
);

  and and_1 (out_9, in_1, in_2);
  and and_2 (out_10, in_3, in_4);
  and and_3 (out_11, in_5, in_6);
  and and_4 (out_12, in_7, in_8);
endmodule

module ic_7404 (
  input  in_1,
  input  in_2,
  input  in_3,
  input  in_4,
  input  in_5,
  input  in_6,
  output out_7,
  output out_8,
  output out_9,
  output out_10,
  output out_11,
  output out_12
);

  not not_1 (out_7, in_1);
  not not_2 (out_8, in_2);
  not not_3 (out_9, in_3);
  not not_4 (out_10, in_4);
  not not_5 (out_11, in_5);
  not not_6 (out_12, in_6);
endmodule

module ic_7432 (
  input  in_1,
  input  in_2,
  input  in_3,
  input  in_4,
  input  in_5,
  input  in_6,
  input  in_7,
  input  in_8,
  output out_9,
  output out_10,
  output out_11,
  output out_12
);

  or or_1 (out_9, in_1, in_2);
  or or_2 (out_10, in_3, in_4);
  or or_3 (out_11, in_5, in_6);
  or or_4 (out_12, in_7, in_8);
endmodule
