// Logisim project 4 Bit Binary Adder-Subtractor.circ as structural Verilog: 2 circuits, main circuit main
module main (
  input  M,
  input  A1,
  input  A2,
  input  A3,
  input  A4,
  input  B1,
  input  B2,
  input  B3,
  input  B4,
  output [3:0] out_10,
  output out_11
);

  wire adder_1_cout, adder_2_cout, adder_3_cout, ic7486_1_out_9, ic7486_1_out_10, ic7486_1_out_11,
       ic7486_1_out_12;

  ic7486 ic7486_1 (
    .in_1(M), .in_2(B1), .in_3(M), .in_4(B2), .in_5(M), .in_6(B4), .in_7(M), .in_8(B3),
    .out_9(ic7486_1_out_9), .out_10(ic7486_1_out_10), .out_11(ic7486_1_out_11), .out_12(ic7486_1_out_12));
  Adder #(.width(1)) adder_1 (.a(A4), .b(ic7486_1_out_11), .out(out_10[0]), .cin(M), .cout(adder_1_cout));
  Adder #(.width(1)) adder_2 (.a(A3), .b(ic7486_1_out_12), .out(out_10[1]), .cin(adder_1_cout), .cout(adder_2_cout));
  Adder #(.width(1)) adder_3 (.a(A2), .b(ic7486_1_out_10), .out(out_10[2]), .cin(adder_2_cout), .cout(adder_3_cout));
  Adder #(.width(1)) adder_4 (.a(A1), .b(ic7486_1_out_9), .out(out_10[3]), .cin(adder_3_cout), .cout(out_11));
endmodule

module ic7486 (
  input  in_1,
  input  in_2,
  input  in_3,
  input  in_4,
  input  in_5,
  input  in_6,
  input  in_7,
  input  in_8,
  output out_9,
  output out_10,
  output out_11,
  output out_12
);

  xor xor_1 (out_9, in_1, in_2);
  xor xor_2 (out_10, in_3, in_4);
  xor xor_3 (out_11, in_5, in_6);
  xor xor_4 (out_12, in_7, in_8);
endmodule
