// Logisim project BCD Adder.circ as structural Verilog: 4 circuits, main circuit main
module main (
  input  A4,
  input  A3,
  input  A2,
  input  A1,
  input  B4,
  input  B3,
  input  B2,
  input  B1,
  input  C_in,
  input  in_10,
  output C,
  output out_12,
  output out_13,
  output out_14,
  output out_15
);

  wire ic7408_1_out_11, ic7408_1_out_12, ic7432_1_out_12, ic74283_1_out_10, ic74283_1_out_11,
       ic74283_1_out_12, ic74283_1_out_13, ic74283_1_out_14;

  ic7408 ic7408_1 (
    .in_5(ic74283_1_out_13), .in_6(ic74283_1_out_11), .in_7(ic74283_1_out_12), .in_8(ic74283_1_out_13),
    .out_11(ic7408_1_out_11), .out_12(ic7408_1_out_12));  // open: in_1, in_2, in_3, in_4, out_9, out_10
  ic74283 ic74283_1 (
    .A1(A1), .B1(B1), .A2(A2), .B2(B2), .A3(A3), .B3(B3), .A4(A4), .B4(B4), .out_10(ic74283_1_out_10),
    .out_11(ic74283_1_out_11), .out_12(ic74283_1_out_12), .out_13(ic74283_1_out_13), .in_1(C_in),
    .out_14(ic74283_1_out_14));
  ic7432 ic7432_1 (
    .in_1(ic7432_1_out_12), .in_2(ic74283_1_out_14), .in_7(ic7408_1_out_12), .in_8(ic7408_1_out_11),
    .out_9(C), .out_12(ic7432_1_out_12));  // open: in_3, in_4, in_5, in_6, out_10, out_11
  ic74283 ic74283_2 (
    .A1(in_10), .B1(ic74283_1_out_10), .A2(C), .B2(ic74283_1_out_11), .A3(C), .B3(ic74283_1_out_12),
    .A4(in_10), .B4(ic74283_1_out_13), .out_10(out_15), .out_11(out_14), .out_12(out_13), .out_13(out_12),
    .in_1(C_in));  // open: out_14

  // Notes on the sheet:
  //   C out
endmodule

module ic74283 (
  input  in_1,
  input  A1,
  input  B1,
  input  A2,
  input  B2,
  input  A3,
  input  B3,
  input  A4,
  input  B4,
  output out_10,
  output out_11,
  output out_12,
  output out_13,
  output out_14
);

  wire adder_1_cout, adder_2_cout, adder_3_cout;

  Adder #(.width(1)) adder_1 (.a(A1), .b(B1), .out(out_10), .cin(in_1), .cout(adder_1_cout));
  Adder #(.width(1)) adder_2 (.a(A2), .b(B2), .out(out_11), .cin(adder_1_cout), .cout(adder_2_cout));
  Adder #(.width(1)) adder_3 (.a(A3), .b(B3), .out(out_12), .cin(adder_2_cout), .cout(adder_3_cout));
  Adder #(.width(1)) adder_4 (.a(A4), .b(B4), .out(out_13), .cin(adder_3_cout), .cout(out_14));
endmodule

module ic7408 (
  input  in_1,
  input  in_2,
  input  in_3,
  input  in_4,
  input  in_5,
  input  in_6,
  input  in_7,
  input  in_8,
  output out_9,
  output out_10,
  output out_11,
  output out_12
);

  and and_1 (out_9, in_1, in_2);
  and and_2 (out_10, in_3, in_4);
  and and_3 (out_11, in_5, in_6);
  and and_4 (out_12, in_7, in_8);
endmodule

module ic7432 (
  input  in_1,
  input  in_2,
  input  in_3,
  input  in_4,
  input  in_5,
  input  in_6,
  input  in_7,
  input  in_8,
  output out_9,
  output out_10,
  output out_11,
  output out_12
);

  or or_1 (out_9, in_1, in_2);
  or or_2 (out_10, in_3, in_4);
  or or_3 (out_11, in_5, in_6);
  or or_4 (out_12, in_7, in_8);
endmodule
