// Logisim project 4 By 1 Multiplexer with Enabler.circ as structural Verilog: 1 circuit, main circuit main
module main (
  input  E,
  input  I_0,
  input  I_1,
  input  I_2,
  input  I_3,
  input  S_1,
  input  S_0,
  output out_8
);

  wire and_1_out, and_2_out, and_3_out, and_4_out, not_1_out, not_2_out, or_1_out, or_2_out;

  not not_1 (not_1_out, S_1);
  not not_2 (not_2_out, S_0);
  and and_1 (and_1_out, E, I_0, not_1_out, not_2_out);
  and and_2 (and_2_out, E, I_1, not_1_out, S_0);
  and and_3 (and_3_out, E, I_2, S_1, not_2_out);
  and and_4 (and_4_out, E, I_3, S_1, S_0);
  or or_1 (or_1_out, and_1_out, and_2_out);
  or or_2 (or_2_out, and_3_out, and_4_out);
  or or_3 (out_8, or_1_out, or_2_out);

  // Notes on the sheet:
  //   4 By 1 Multiplexer with Enabler
endmodule
