// Logisim project 8 By 1 Multiplexer.circ as structural Verilog: 1 circuit, main circuit main
module main (
  input  in_1,
  input  in_2,
  input  E,
  input  [2:0] ABC,
  input  D,
  output out_6
);

  Multiplexer #(.select(3)) multiplexer_1 (
    .in0(in_2), .in1(D), .in2(D), .in3(in_1), .in4(in_2), .in5(in_1), .in6(in_1), .in7(in_2), .out(out_6),
    .sel(ABC), .en(E));

  // Notes on the sheet:
  //   8:1 Multiplexer
endmodule
